# Fritzing sketch 802e8d14-bff5-42b7-b4ba-8c4048279907 (saved by Fritzing 0.9.3b)
breadboards: 1

parts:
  LED1 = smd LED [color="Green (555nm)" package="0805 [SMD]"]
  Part1 = Arduino Uno (Rev3) - ICSP
  LED2 = LED - 5mm [color="Red (633nm)" package="5 mm [THT]"]
  R1 = Resistor [tolerance=±5% resistance=220 package=THT]
  R2 = Resistor [tolerance=±5% resistance=220 package=THT]

nets:
  N1: LED1.cathode, LED2.cathode
  N2: LED1.anode, R2.Pin_0
  N3: Part1.D3_PWM, R1.Pin_1
  N4: Part1.D4, R2.Pin_1
  N5: LED2.anode, R1.Pin_0
